# Fritzing sketch As_Built_Lesson_1 (saved by Fritzing 1.0.2b)
circuit board: 8.46667cm x 5.64444cm
breadboards: 1

parts:
  Mod1 = Raspberry Pi Pico W
  R1 = Resistor [tolerance=±5% power=0.25W resistance=220k package=THT]
  LED2 = LED - 5mm [color="Yellow (592nm)" current=0.030A package="5 mm [THT]"]
  LED1 = LED - 5mm [color="Red (633nm)" current=0.030A package="5 mm [THT]"]
  R2 = Resistor [tolerance=±5% power=0.25W resistance=220k package=THT]
  R3 = Resistor [tolerance=±5% power=0.25W resistance=220k package=THT]
  LED3 = LED - 5mm [color="Green (560nm)" current=0.030A package="5 mm [THT]"]

nets:
  N1: Mod1.pin_3, Mod1.pin_8, Mod1.pin_13, Mod1.pin_18, Mod1.pin_23, Mod1.pin_28, Mod1.pin_33, Mod1.pin_38, LED2.cathode, LED1.cathode, LED3.cathode
  N2: Mod1.pin_21, R1.Pin_1
  N3: Mod1.pin_22, R2.Pin_0
  N4: Mod1.pin_24, R3.Pin_0
  N5: R1.Pin_0, LED1.anode
  N6: LED2.anode, R2.Pin_1
  N7: R3.Pin_1, LED3.anode

custom parts:
  Raspberry Pi Pico W: Raspberry Pi Pico W. Based around the RP2040 microcontroller the Pico W is a low cost microcontroller device bringing Raspberry Pi quality, cost, and easy of use to the microcontroller space. The areas marked KEEPOUT in pcb silkscreen should not have traces running through them to avoid shorts on a soldered in module!
