# Fritzing sketch Lesson_3 (saved by Fritzing 1.0.2b)
circuit board: 8.46667cm x 5.64444cm
breadboards: 1

parts:
  Mod1 = Raspberry Pi Pico W
  R1 = Resistor [tolerance=±10% power=0.25W resistance=10k package=THT]
  R2 = Resistor [tolerance=±10% power=0.25W resistance=220 package=THT]
  R3 = Photocell (LDR) [power=0.25W dark_resistance_@0.01lx=300kΩ light_resistance_@100lx=400Ω luminance=10lx package=THT]
  LED1 = LED - 5mm [color="Green (565nm)" current=0.030A package="5 mm [THT]"]

nets:
  N1: Mod1.pin_3, Mod1.pin_8, Mod1.pin_13, Mod1.pin_18, Mod1.pin_23, Mod1.pin_28, Mod1.pin_33, Mod1.pin_38, R1.Pin_0, LED1.cathode
  N2: Mod1.pin_22, R2.Pin_0
  N3: Mod1.pin_32, R1.Pin_1, R3.pin_0
  N4: Mod1.pin_35, R3.pin_1
  N5: R2.Pin_1, LED1.anode

custom parts:
  Raspberry Pi Pico W: Raspberry Pi Pico W. Based around the RP2040 microcontroller the Pico W is a low cost microcontroller device bringing Raspberry Pi quality, cost, and easy of use to the microcontroller space. The areas marked KEEPOUT in pcb silkscreen should not have traces running through them to avoid shorts on a soldered in module!
