# Fritzing sketch Lesson_4-ChatGPT (saved by Fritzing 1.0.2b)
breadboards: 1

parts:
  Mod1 = Raspberry Pi Pico W
  S1 = Pushbutton [package="[THT]"]
  R1 = Resistor [tolerance=±10% power=0.25W resistance=10k package=THT]
  R2 = Resistor [tolerance=±5% power=0.25W resistance=220 package=THT]
  LED1 = LED - 5mm [color="Green (560nm)" current=0.030A package="5 mm [THT]"]

nets:
  N1: Mod1.pin_3, Mod1.pin_8, Mod1.pin_13, Mod1.pin_18, Mod1.pin_23, Mod1.pin_28, Mod1.pin_33, Mod1.pin_38, Mod1.pin_42, R1.Pin_1, R2.Pin_1
  N2: Mod1.pin_19, LED1.anode
  N3: Mod1.pin_20, S1.Pin_3, S1.Pin_4, R1.Pin_0
  N4: Mod1.pin_36, S1.Pin_1, S1.Pin_2
  N5: R2.Pin_0, LED1.cathode

custom parts:
  Raspberry Pi Pico W: Raspberry Pi Pico W. Based around the RP2040 microcontroller the Pico W is a low cost microcontroller device bringing Raspberry Pi quality, cost, and easy of use to the microcontroller space. The areas marked KEEPOUT in pcb silkscreen should not have traces running through them to avoid shorts on a soldered in module!
