# Fritzing sketch Lesson_6 (saved by Fritzing 1.0.2b)
circuit board: 8.46667cm x 5.64444cm
breadboards: 1

parts:
  Mod1 = Raspberry Pi Pico W
  S1 = Pushbutton [package="[THT]"]
  R5 = Resistor [tolerance=±10% power=0.25W resistance=10k package=THT]
  R2 = Resistor [tolerance=±5% power=0.25W resistance=220 package=THT]
  R1 = Resistor [tolerance=±5% power=0.25W resistance=220 package=THT]
  R3 = Resistor [tolerance=±5% power=0.25W resistance=220 package=THT]
  R4 = Resistor [tolerance=±5% power=0.25W resistance=220 package=THT]
  LED1 = LED - 5mm [color="Green (560nm)" current=0.030A package="5 mm [THT]"]
  LED2 = LED - 5mm [color="Green (560nm)" current=0.030A package="5 mm [THT]"]
  LED3 = LED - 5mm [color="Green (560nm)" current=0.030A package="5 mm [THT]"]
  LED4 = LED - 5mm [color="Green (560nm)" current=0.030A package="5 mm [THT]"]

nets:
  N1: Mod1.pin_1, R1.Pin_0
  N2: Mod1.pin_2, R2.Pin_0
  N3: Mod1.pin_3, Mod1.pin_8, Mod1.pin_13, Mod1.pin_18, Mod1.pin_23, Mod1.pin_28, Mod1.pin_33, Mod1.pin_38, Mod1.pin_42, R5.Pin_1, LED1.cathode, LED2.cathode, LED3.cathode, LED4.cathode
  N4: Mod1.pin_4, R3.Pin_0
  N5: Mod1.pin_5, R4.Pin_0
  N6: Mod1.pin_11, S1.Pin_1, S1.Pin_2, R5.Pin_0
  N7: Mod1.pin_36, S1.Pin_3, S1.Pin_4
  N8: R2.Pin_1, LED2.anode
  N9: R1.Pin_1, LED1.anode
  N10: R3.Pin_1, LED3.anode
  N11: R4.Pin_1, LED4.anode

custom parts:
  Raspberry Pi Pico W: Raspberry Pi Pico W. Based around the RP2040 microcontroller the Pico W is a low cost microcontroller device bringing Raspberry Pi quality, cost, and easy of use to the microcontroller space. The areas marked KEEPOUT in pcb silkscreen should not have traces running through them to avoid shorts on a soldered in module!
